# Fritzing sketch Smart Mobil (saved by Fritzing 0.9.3b)

parts:
  Part1 = Arduino Uno (Rev3)
  BT1 = Bluetooth HC-06u [package=THT]
  M3 = DC Motor
  VCC4 = Battery block 9V
  VCC5 = Battery block 9V
  S1 = H-Bridge with L298N
  M5 = DC Motor
  R2 = Resistor [tolerance=±5% resistance=680 package="0805 [SMD]"]
  R3 = Resistor [tolerance=±5% resistance=303 package="0805 [SMD]"]
  JACK1 = 2.1mm Barrel Jack with Terminal Block

nets:
  N1: Part1.GND, R2.Pin_1
  N2: Part1.D3_PWM, BT1.TXD
  N3: Part1.D4, R3.Pin_0
  5V: Part1.5V, BT1.VCC
  N4: BT1.RXD, R3.Pin_1
  N5: M3.pin_1, S1.M1-02
  N6: M3.pin_2, S1.M1-01
  N7: VCC4.-, S1.GND
  N8: VCC4.+, S1.12V
  N9: VCC5.-, JACK1.NEG
  N10: VCC5.+, JACK1.POS
  N11: S1.M2-01, M5.pin_2
  N12: S1.M2-02, M5.pin_1

custom parts:
  Bluetooth HC-06u: Bluetooth HC-06 - face up, pins down 16.5mm x 37.5mm PCB
  H-Bridge with L298N: h-bridge
